# Fritzing sketch Shieldv0 (saved by Fritzing 0.6.4b)
breadboards: 1

parts:
  Arduino1 = Arduino
  LED1 = LED - 5mm [color="Red (635nm)" package="5 mm [THT]"]
  LED2 = RGB LED (com. cathode, rbg) [package="5 mm [THT]"]
  LED3 = LED - 5mm [color="Yellow (595nm)" package="5 mm [THT]"]
  LED4 = LED - 5mm [color="Green (570nm)" package="5 mm [THT]"]
  R1 = Rotary Potentiometer (Small) [maximum_resistance=100kΩ]
  R2 = Trimmer Potentiometer [maximum_resistance=10kΩ package=THT]
  R3 = Photocell (LDR) [package=THT]
  R4 = Trimmer Potentiometer [maximum_resistance=10kΩ package=THT]
  S1 = Pushbutton [package="[THT]"]
  S2 = Pushbutton [package="[THT]"]
  S3 = Pushbutton [package="[THT]"]  # not connected
  T1 = LM35 Temperature Sensor [package="TO92 [THT]"]  # not connected
  LED5 = LED - 5mm [color="Red (633nm)" package="5 mm [THT]"]
  LED6 = LED - 5mm [color="Red (633nm)" package="5 mm [THT]"]
  R5 = Resistor [tolerance=±5% resistance=1k package=THT]
  R6 = Resistor [tolerance=±5% resistance=2.2k package=THT]
  R7 = Trimmer Potentiometer [maximum_resistance=10kΩ package=THT]  # not connected
  LED7 = LED - 5mm [color="Red (633nm)" package="5 mm [THT]"]
  R8 = Resistor [tolerance=±5% resistance=1k package=THT]
  R9 = Resistor [tolerance=±5% resistance=1k package=THT]

nets:
  N1: Arduino1.D13, LED1.anode
  N2: Arduino1.D12, LED3.anode
  N3: Arduino1.D11, LED2.green_anode
  N4: Arduino1.D10, LED2.blue_anode
  N5: Arduino1.D9, LED2.red_anode
  N6: Arduino1.D8, LED4.anode
  N7: Arduino1.D6, LED5.anode
  N8: Arduino1.D5, LED6.anode
  N9: Arduino1.D4, S2.Pin_3, S2.Pin_4, R9.Pin_0
  N10: Arduino1.D3, S1.Pin_3, S1.Pin_4, R9.Pin_1
  N11: Arduino1.D2, LED7.anode
  N12: Arduino1.+5V, R1.leg2, R2.leg2, R3.pin_0, R4.leg2, R6.Pin_0
  N13: Arduino1.GND, LED1.cathode, LED2.common_cathode, LED3.cathode, LED4.cathode, R1.leg1, R2.leg1, R4.leg1, LED5.cathode, LED6.cathode, R5.Pin_1, LED7.cathode, R8.Pin_0
  N14: Arduino1.A0, R3.pin_1, R5.Pin_0
  N15: Arduino1.A1, R1.wiper
  N16: Arduino1.A2, R2.wiper
  N17: Arduino1.A3, R4.wiper
  N18: S1.Pin_1, S1.Pin_2, R8.Pin_1
  N19: S2.Pin_1, S2.Pin_2

notes:
  Rojo: +5V
  Negro: GND
  Amarillo: señal analógica
  Azul: señal OUTPUT/ PWM
  Verde: señal digital (INPUT)
  Blanco: señal digital (OUTPUT)
  SW1 pull down
  SW2 pull up
  SW3 ?
  Propuestas de ejercicios:
  -Semaforo (LEDS)
  -coche fantastico(LEDS)
  -leer temperatura (LM35+SERIE)
  -Vumetro con temperatura(LM35+LEDS)
  -contador binario (LEDS + SWITCH)
  -contador up/down binario (LEDS + 2 SWITCH)
  -lectura LDR
  -control iluminacion (LDR + RGB)
  -cambiar colores RGB (potenciometros+RGB)
