# Fritzing sketch Shieldv2 (saved by Fritzing 0.6.4b)
breadboards: 1

parts:
  By_PepeChorva_&_Jose_Manuel_Escuder = Arduino
  LED1 = LED - 5mm [color="Red (635nm)" package="5 mm [THT]"]
  RGB = RGB LED (com. cathode, rbg) [package="5 mm [THT]"]
  LED3 = LED - 5mm [color="Yellow (595nm)" package="5 mm [THT]"]
  LED4 = LED - 5mm [color="Green (570nm)" package="5 mm [THT]"]
  R1 = Rotary Potentiometer (Small) [maximum_resistance=10kΩ]
  R3 = Photocell (LDR) [package=THT]
  S1 = Pushbutton [package="[THT]"]
  S2 = Pushbutton [package="[THT]"]
  T1 = LM35 Temperature Sensor [package="TO92 [THT]"]
  LED5 = LED - 5mm [color="Red (633nm)" package="5 mm [THT]"]
  LED6 = LED - 5mm [color="Red (633nm)" package="5 mm [THT]"]
  LED7 = LED - 5mm [color="Red (633nm)" package="5 mm [THT]"]
  R10 = Rotary Potentiometer (Small) [maximum_resistance=10kΩ]
  Hall = mystery part, 3 pins [chip_label="Sensor Hall SS29" spacing=300mil]
  R6 = Resistor [tolerance=±5% resistance=2.2k package="1206 [SMD]"]
  R5 = Resistor [tolerance=±5% resistance=1k package="1206 [SMD]"]
  R8 = Resistor [tolerance=±5% resistance=1k package="1206 [SMD]"]
  R9 = Resistor [tolerance=±5% resistance=1k package="1206 [SMD]"]
  J1 = Piezo Speaker
  R11 = Trimmer Potentiometer [maximum_resistance=10kΩ package=THT]

nets:
  N1: By_PepeChorva_&_Jose_Manuel_Escuder.D13, LED1.anode
  N2: By_PepeChorva_&_Jose_Manuel_Escuder.D12, LED3.anode
  N3: By_PepeChorva_&_Jose_Manuel_Escuder.D11, RGB.green_anode
  N4: By_PepeChorva_&_Jose_Manuel_Escuder.D10, RGB.blue_anode
  N5: By_PepeChorva_&_Jose_Manuel_Escuder.D9, RGB.red_anode
  N6: By_PepeChorva_&_Jose_Manuel_Escuder.D8, LED4.anode
  N7: By_PepeChorva_&_Jose_Manuel_Escuder.D7, R11.leg2
  N8: By_PepeChorva_&_Jose_Manuel_Escuder.D6, LED5.anode
  N9: By_PepeChorva_&_Jose_Manuel_Escuder.D5, LED6.anode
  GND: By_PepeChorva_&_Jose_Manuel_Escuder.D4, By_PepeChorva_&_Jose_Manuel_Escuder.GND, LED1.cathode, RGB.common_cathode, LED3.cathode, LED4.cathode, R1.leg1, S2.Pin_3, S2.Pin_4, T1.GND, LED5.cathode, LED6.cathode, LED7.cathode, R10.leg1, Hall.pin2, R5.Pin_1, R8.Pin_0, R9.Pin_0, J1.pin1, R11.leg1
  N10: By_PepeChorva_&_Jose_Manuel_Escuder.D3, By_PepeChorva_&_Jose_Manuel_Escuder.+5V, R1.leg2, R3.pin_0, S1.Pin_3, S1.Pin_4, R10.leg2, Hall.pin1, R6.Pin_0
  N11: By_PepeChorva_&_Jose_Manuel_Escuder.D2, LED7.anode
  N12: By_PepeChorva_&_Jose_Manuel_Escuder.A0, R3.pin_1, R5.Pin_0
  N13: By_PepeChorva_&_Jose_Manuel_Escuder.A1, R1.wiper
  N14: By_PepeChorva_&_Jose_Manuel_Escuder.A2, R10.wiper
  N15: By_PepeChorva_&_Jose_Manuel_Escuder.A3, Hall.pin3
  N16: By_PepeChorva_&_Jose_Manuel_Escuder.A4, T1.Vout
  N17: S1.Pin_1, S1.Pin_2, R8.Pin_1
  N18: S2.Pin_1, S2.Pin_2
  N19: T1.+Vs, R6.Pin_1
  N20: J1.pin2, R11.wiper

notes:
  Rojo: +5V
  Negro: GND
  Amarillo: señal analógica
  Azul: señal OUTPUT/ PWM
  Verde: señal digital (INPUT)
  Blanco: señal digital (OUTPUT)
  SW1 pull down
  SW2 pull up
  Propuestas de ejercicios:
  -Semaforo (LEDS)
  -coche fantastico(LEDS)
  -leer temperatura (LM35+SERIE)
  -Vumetro con temperatura(LM35+LEDS)
  -contador binario (LEDS + SWITCH)
  -contador up/down binario (LEDS + 2 SWITCH)
  -lectura LDR
  -control iluminacion (LDR + RGB)
  -cambiar colores RGB (potenciometros+RGB)
