# Fritzing sketch Shieldv3 (saved by Fritzing 0.6.4b)
breadboards: 1

parts:
  By_PepeChorva = Arduino
  LED1 = LED - 5mm [color="Red (635nm)" package="5 mm [THT]"]
  RGB = RGB LED (com. cathode, rbg) [package="5 mm [THT]"]
  LED3 = LED - 5mm [color="Yellow (595nm)" package="5 mm [THT]"]
  LED4 = LED - 5mm [color="Green (570nm)" package="5 mm [THT]"]
  R1 = Rotary Potentiometer (Small) [maximum_resistance=10kΩ]
  R3 = Photocell (LDR) [package=THT]
  S1 = Pushbutton [package="[THT]"]
  S2 = Pushbutton [package="[THT]"]
  T1 = LM35 Temperature Sensor [package="TO92 [THT]"]
  LED5 = LED - 5mm [color="Red (633nm)" package="5 mm [THT]"]
  LED6 = LED - 5mm [color="Red (633nm)" package="5 mm [THT]"]
  LED7 = LED - 5mm [color="Red (633nm)" package="5 mm [THT]"]
  R10 = Rotary Potentiometer (Small) [maximum_resistance=10kΩ]
  Hall = mystery part, 3 pins [chip_label="Sensor Hall SS29" spacing=300mil]
  R6 = Resistor [tolerance=±5% resistance=2.2k package="1206 [SMD]"]
  R5 = Resistor [tolerance=±5% resistance=1k package="1206 [SMD]"]
  R8 = Resistor [tolerance=±5% resistance=220 package="1206 [SMD]"]
  R9 = Resistor [tolerance=±5% resistance=10k package="1206 [SMD]"]
  BUZZER = Piezo Speaker

nets:
  GND: By_PepeChorva.GND, By_PepeChorva.A2, LED1.cathode, RGB.common_cathode, LED3.cathode, LED4.cathode, R1.leg1, T1.GND, LED5.cathode, LED6.cathode, LED7.cathode, R10.leg1, R10.wiper, Hall.pin2, R5.Pin_1, R8.Pin_0, BUZZER.pin1
  N1: By_PepeChorva.D13, LED1.anode
  N2: By_PepeChorva.D12, LED3.anode
  N3: By_PepeChorva.D11, RGB.green_anode
  N4: By_PepeChorva.D10, RGB.blue_anode
  N5: By_PepeChorva.D9, RGB.red_anode
  N6: By_PepeChorva.D8, LED4.anode
  N7: By_PepeChorva.D7, BUZZER.pin2
  N8: By_PepeChorva.D6, LED5.anode
  N9: By_PepeChorva.D5, LED6.anode
  N10: By_PepeChorva.D4, S2.Pin_3, S2.Pin_4, R9.Pin_0
  N11: By_PepeChorva.D3, S1.Pin_3, S1.Pin_4, R9.Pin_1
  N12: By_PepeChorva.D2, LED7.anode
  N13: By_PepeChorva.+5V, R1.leg2, R3.pin_0, R10.leg2, Hall.pin1, R6.Pin_0
  N14: By_PepeChorva.A0, R3.pin_1, R5.Pin_0
  N15: By_PepeChorva.A1, R1.wiper
  N16: By_PepeChorva.A3, Hall.pin3
  N17: By_PepeChorva.A4, T1.Vout
  N18: S1.Pin_1, S1.Pin_2, R8.Pin_1
  N19: S2.Pin_1, S2.Pin_2
  N20: T1.+Vs, R6.Pin_1

notes:
  Rojo: +5V
  Negro: GND
  Amarillo: señal analógica
  Azul: señal OUTPUT/ PWM
  Verde: señal digital (INPUT)
  Blanco: señal digital (OUTPUT)
  SW1 pull down
  SW2 pull up
  SW3 ?
  Propuestas de ejercicios:
  -Semaforo (LEDS)
  -coche fantastico(LEDS)
  -leer temperatura (LM35+SERIE)
  -Vumetro con temperatura(LM35+LEDS)
  -contador binario (LEDS + SWITCH)
  -contador up/down binario (LEDS + 2 SWITCH)
  -lectura LDR
  -control iluminacion (LDR + RGB)
  -cambiar colores RGB (potenciometros+RGB)
