# Fritzing sketch Shieldv4 (saved by Fritzing 0.6.4b)
breadboards: 1

parts:
  Pepe_Chorva_&_Jose_Manuel_Escuder = Arduino
  LED2 = LED - 5mm [color="Red (635nm)" package="5 mm [THT]"]
  LED3 = LED - 5mm [color="Red (635nm)" package="5 mm [THT]"]
  LED4 = LED - 5mm [color="Yellow (592nm)" package="5 mm [THT]"]
  LED5 = LED - 5mm [color="Green (555nm)" package="5 mm [THT]"]
  RGB = RGB LED (com. cathode, rbg) [package="5 mm [THT]"]
  SW1 = Pushbutton [package="[THT]"]
  BUZZER = Piezo Speaker
  Sens1 = LM35 Temperature Sensor [package="TO92 [THT]"]
  POT2 = Rotary Potentiometer (Small) [maximum_resistance=10kΩ]
  POT1 = Rotary Potentiometer (Small) [maximum_resistance=10kΩ]
  R1 = Resistor [tolerance=±5% resistance=220 package="1206 [SMD]"]
  LDR = Photocell (LDR) [package=THT]
  R2 = Resistor [tolerance=±5% resistance=1k package="1206 [SMD]"]
  R4 = Resistor [tolerance=±5% resistance=1k package="1206 [SMD]"]
  R3 = Resistor [tolerance=±5% resistance=1k package="1206 [SMD]"]
  LED1 = LED - 5mm [color="Red (635nm)" package="5 mm [THT]"]
  R5 = Resistor [tolerance=±5% resistance=4.7k package="1206 [SMD]"]
  POT3 = Trimmer Potentiometer [maximum_resistance=10kΩ package=THT]
  SW2 = Pushbutton [package="[THT]"]
  SW3 = Pushbutton [package="[THT]"]

nets:
  GND: Pepe_Chorva_&_Jose_Manuel_Escuder.GND, LED2.cathode, LED3.cathode, LED4.cathode, LED5.cathode, RGB.common_cathode, BUZZER.pin1, Sens1.GND, POT2.leg1, POT1.leg1, R2.Pin_0, R4.Pin_0, R3.Pin_0, LED1.cathode, POT3.leg2, SW3.Pin_1, SW3.Pin_2
  N1: Pepe_Chorva_&_Jose_Manuel_Escuder.D13, SW1.Pin_3, SW1.Pin_4, R3.Pin_1
  N2: Pepe_Chorva_&_Jose_Manuel_Escuder.D12, R4.Pin_1, SW2.Pin_3, SW2.Pin_4
  N3: Pepe_Chorva_&_Jose_Manuel_Escuder.D11, RGB.red_anode
  N4: Pepe_Chorva_&_Jose_Manuel_Escuder.D10, RGB.blue_anode
  N5: Pepe_Chorva_&_Jose_Manuel_Escuder.D9, RGB.green_anode
  N6: Pepe_Chorva_&_Jose_Manuel_Escuder.D8, R5.Pin_1, SW3.Pin_3, SW3.Pin_4
  N7: Pepe_Chorva_&_Jose_Manuel_Escuder.D7, LED1.anode
  N8: Pepe_Chorva_&_Jose_Manuel_Escuder.D6, LED2.anode
  N9: Pepe_Chorva_&_Jose_Manuel_Escuder.D5, LED3.anode
  N10: Pepe_Chorva_&_Jose_Manuel_Escuder.D4, LED4.anode
  N11: Pepe_Chorva_&_Jose_Manuel_Escuder.D3, POT3.leg1
  N12: Pepe_Chorva_&_Jose_Manuel_Escuder.D2, LED5.anode
  N13: Pepe_Chorva_&_Jose_Manuel_Escuder.+5V, SW1.Pin_1, SW1.Pin_2, POT2.leg2, POT1.leg2, R1.Pin_1, LDR.pin_1, R5.Pin_0, SW2.Pin_1, SW2.Pin_2
  N14: Pepe_Chorva_&_Jose_Manuel_Escuder.A0, POT1.wiper
  N15: Pepe_Chorva_&_Jose_Manuel_Escuder.A1, POT2.wiper
  N16: Pepe_Chorva_&_Jose_Manuel_Escuder.A2, Sens1.Vout
  N17: Pepe_Chorva_&_Jose_Manuel_Escuder.A3, LDR.pin_0, R2.Pin_1
  N18: BUZZER.pin2, POT3.wiper
  N19: Sens1.+Vs, R1.Pin_0

notes:
  Rojo: +5V
  Negro: GND
  Amarillo: señal analógica
  Azul: señal OUTPUT/ PWM
  Verde: señal digital (INPUT)
  Blanco: señal digital (OUTPUT)
  SW1 pull down
  SW2 pull up
  Propuestas de ejercicios:
  -Semaforo (LEDS)
  -coche fantastico(LEDS)
  -leer temperatura (LM35+SERIE)
  -Vumetro con temperatura(LM35+LEDS)
  -contador binario (LEDS + SWITCH)
  -contador up/down binario (LEDS + 2 SWITCH)
  -lectura LDR
  -control iluminacion (LDR + RGB)
  -cambiar colores RGB (potenciometros+RGB)
