# Fritzing sketch Shieldv5 (saved by Fritzing 0.6.4b)
breadboards: 1

parts:
  LED2 = LED - 5mm [color="Red (635nm)" package="5 mm [THT]"]
  LED3 = LED - 5mm [color="Red (635nm)" package="5 mm [THT]"]
  LED4 = LED - 5mm [color="Yellow (592nm)" package="5 mm [THT]"]
  LED5 = LED - 5mm [color="Green (555nm)" package="5 mm [THT]"]
  RGB = RGB LED (com. cathode, rbg) [package="5 mm [THT]"]
  SW1 = Pushbutton [package="[THT]"]
  Sens1 = LM35 Temperature Sensor [package="TO92 [THT]"]
  POT2 = Rotary Potentiometer (Small) [maximum_resistance=10kΩ]
  POT1 = Rotary Potentiometer (Small) [maximum_resistance=10kΩ]
  R1 = Resistor [tolerance=±5% resistance=220 package="1206 [SMD]"]
  LDR = Photocell (LDR) [package=THT]
  R2 = Resistor [tolerance=±5% resistance=1k package="1206 [SMD]"]
  R4 = Resistor [tolerance=±5% resistance=1k package="1206 [SMD]"]
  R3 = Resistor [tolerance=±5% resistance=1k package="1206 [SMD]"]
  LED1 = LED - 5mm [color="Red (635nm)" package="5 mm [THT]"]
  R5 = Resistor [tolerance=±5% resistance=4.7k package="1206 [SMD]"]
  POT3 = Trimmer Potentiometer [maximum_resistance=10kΩ package=THT]
  SW2 = Pushbutton [package="[THT]"]
  SW3 = Pushbutton [package="[THT]"]
  R6 = Resistor [tolerance=±5% resistance=220 package="1206 [SMD]"]
  R7 = Resistor [tolerance=±5% resistance=220 package="1206 [SMD]"]
  R8 = Resistor [tolerance=±5% resistance=220 package="1206 [SMD]"]
  R9 = Resistor [tolerance=±5% resistance=220 package="1206 [SMD]"]
  R10 = Resistor [tolerance=±5% resistance=220 package="1206 [SMD]"]
  R11 = Resistor [tolerance=±5% resistance=220 package="1206 [SMD]"]
  R12 = Resistor [tolerance=±5% resistance=220 package="1206 [SMD]"]
  R13 = Resistor [tolerance=±5% resistance=220 package="1206 [SMD]"]
  Pepe_Chorva_&_Jose_Manuel_Escuder = Arduino
  BUZZER = Piezo Speaker

nets:
  N1: LED2.cathode, LED3.cathode, LED4.cathode, LED5.cathode, RGB.common_cathode, LED1.cathode
  N2: LED2.anode, R10.Pin_0
  N3: LED3.anode, R11.Pin_0
  N4: LED4.anode, R12.Pin_0
  N5: LED5.anode, R13.Pin_0
  N6: RGB.red_anode, R6.Pin_0
  N7: RGB.blue_anode, R7.Pin_0
  N8: RGB.green_anode, R8.Pin_0
  N9: SW1.Pin_1, SW1.Pin_2, POT2.leg2, POT1.leg2, R1.Pin_1, LDR.pin_1, R5.Pin_0, SW2.Pin_1, SW2.Pin_2, Pepe_Chorva_&_Jose_Manuel_Escuder.+5V
  N10: SW1.Pin_3, SW1.Pin_4, R3.Pin_1, Pepe_Chorva_&_Jose_Manuel_Escuder.D13
  N11: Sens1.+Vs, R1.Pin_0
  N12: Sens1.Vout, Pepe_Chorva_&_Jose_Manuel_Escuder.A2
  GND: Sens1.GND, POT2.leg1, POT1.leg1, R2.Pin_0, R4.Pin_0, R3.Pin_0, POT3.leg2, SW3.Pin_1, SW3.Pin_2, Pepe_Chorva_&_Jose_Manuel_Escuder.GND, BUZZER.pin1
  N13: POT2.wiper, Pepe_Chorva_&_Jose_Manuel_Escuder.A1
  N14: POT1.wiper, Pepe_Chorva_&_Jose_Manuel_Escuder.A0
  N15: LDR.pin_0, R2.Pin_1, Pepe_Chorva_&_Jose_Manuel_Escuder.A3
  N16: R4.Pin_1, SW2.Pin_3, SW2.Pin_4, Pepe_Chorva_&_Jose_Manuel_Escuder.D12
  N17: LED1.anode, R9.Pin_0
  N18: R5.Pin_1, SW3.Pin_3, SW3.Pin_4, Pepe_Chorva_&_Jose_Manuel_Escuder.D8
  N19: POT3.leg1, Pepe_Chorva_&_Jose_Manuel_Escuder.D3
  N20: POT3.wiper, BUZZER.pin2
  N21: R6.Pin_1, Pepe_Chorva_&_Jose_Manuel_Escuder.D11
  N22: R7.Pin_1, Pepe_Chorva_&_Jose_Manuel_Escuder.D10
  N23: R8.Pin_1, Pepe_Chorva_&_Jose_Manuel_Escuder.D9
  N24: R9.Pin_1, Pepe_Chorva_&_Jose_Manuel_Escuder.D7
  N25: R10.Pin_1, Pepe_Chorva_&_Jose_Manuel_Escuder.D6
  N26: R11.Pin_1, Pepe_Chorva_&_Jose_Manuel_Escuder.D5
  N27: R12.Pin_1, Pepe_Chorva_&_Jose_Manuel_Escuder.D4
  N28: R13.Pin_1, Pepe_Chorva_&_Jose_Manuel_Escuder.D2

notes:
  Rojo: +5V
  Negro: GND
  Amarillo: señal analógica
  Azul: señal OUTPUT/ PWM
  Verde: señal digital (INPUT)
  Blanco: señal digital (OUTPUT)
  SW1 pull down
  SW2 pull down
  SW3 pull up
  Propuestas de ejercicios:
  -Semaforo (LEDS)
  -coche fantastico(LEDS)
  -leer temperatura (LM35+SERIE)
  -Vumetro con temperatura(LM35+LEDS)
  -contador binario (LEDS + SWITCH)
  -contador up/down binario (LEDS + 2 SWITCH)
  -lectura LDR
  -control iluminacion (LDR + RGB)
  -cambiar colores RGB (potenciometros+RGB)
  practDuino
