# Fritzing sketch RGB (saved by Fritzing 0.6.4b)
breadboards: 1

parts:
  RGB = RGB LED (com. cathode, rbg) [package="5 mm [THT]"]
  R6 = Resistor [tolerance=±5% resistance=220 package="1206 [SMD]"]
  R7 = Resistor [tolerance=±5% resistance=220 package="1206 [SMD]"]
  R8 = Resistor [tolerance=±5% resistance=220 package="1206 [SMD]"]
  Pepe_Chorva_&_Jose_Manuel_Escuder = Arduino

nets:
  N1: RGB.red_anode, R6.Pin_0
  N2: RGB.common_cathode, Pepe_Chorva_&_Jose_Manuel_Escuder.GND
  N3: RGB.blue_anode, R7.Pin_0
  N4: RGB.green_anode, R8.Pin_0
  N5: R6.Pin_1, Pepe_Chorva_&_Jose_Manuel_Escuder.D11
  N6: R7.Pin_1, Pepe_Chorva_&_Jose_Manuel_Escuder.D10
  N7: R8.Pin_1, Pepe_Chorva_&_Jose_Manuel_Escuder.D9

notes:
  Rojo: +5V
  Negro: GND
  Amarillo: señal analógica
  Azul: señal OUTPUT/ PWM
  Verde: señal digital (INPUT)
  Blanco: señal digital (OUTPUT)
  SW1 pull down
  SW2 pull down
  SW3 pull up
  Propuestas de ejercicios:
  -Semaforo (LEDS)
  -coche fantastico(LEDS)
  -leer temperatura (LM35+SERIE)
  -Vumetro con temperatura(LM35+LEDS)
  -contador binario (LEDS + SWITCH)
  -contador up/down binario (LEDS + 2 SWITCH)
  -lectura LDR
  -control iluminacion (LDR + RGB)
  -cambiar colores RGB (potenciometros+RGB)
  practDuino
